# Fritzing sketch RRFDisplayTiny (saved by Fritzing 0.9.2b)
breadboards: 1

parts:
  S1 = Momentary Switch [package=ksa_sealed_tac_switch]
  R1 = Resistor [tolerance=±5% resistance=10k package="2010 [SMD]"]
  U2 = LIPO-1000mAh [package=lipo-1000]  # not connected

nets:
  N1: S1.1, S1.2, R1.Pin_0
  N2: S1.3, S1.4
